# Fritzing sketch Arduino Sumo Mark 3 v2 (saved by Fritzing 0.9.1b)
circuit board: 6.54844cm x 5.7231cm
breadboards: 1

parts:
  JP4 = Header 1 [package=1x01_offset]
  JP5 = Header 1 [package=1x01_offset]
  QRB1134 = Header 1 [package=1x01_offset]
  JP7 = Header 1 [package=1x01_offset]
  JP9 = Header 1 [package=1x01_offset]
  QRB1134_2 = Header 1 [package=1x01_offset]
  JP11 = Header 1 [package=1x01_offset]
  JP12 = Header 1 [package=1x01_offset]
  JP13 = Header 1 [package=1x01_offset]
  QRB1134_3 = Header 1 [package=1x01_offset]
  0_1 = Capacitor [package=cap-pth-small2]
  0_1_2 = Capacitor [package=cap-pth-small2]
  11 = LED - 3mm [color="Red (633nm)" package="3 mm [THT]"]
  Part1 = Arduino Leonardo (Rev3b)
  13 = LED - 3mm [color="Red (633nm)" package="3 mm [THT]"]
  12 = LED - 3mm [color="Red (633nm)" package="3 mm [THT]"]
  0_1_3 = Capacitor [package=cap-pth-small2]
  10k = Resistor [tolerance=±5% resistance=220 package=THT]
  220 = Resistor [tolerance=±5% resistance=220 package=THT]
  10k_2 = Resistor [tolerance=±5% resistance=220 package=THT]
  220_2 = Resistor [tolerance=±5% resistance=220 package=THT]
  10k_3 = Resistor [tolerance=±5% resistance=220 package=THT]
  2YOA21 = Header 3 [package=jst-3-pth]
  2YOA21_2 = Header 3 [package=jst-3-pth]
  Bat = Screw terminal - 2 pins [package=THT]
  470 = Resistor [tolerance=±5% resistance=220 package=THT]
  On_Off = SPST Switch [package=switch-spdt_kit]
  220_3 = Resistor [tolerance=±5% resistance=220 package=THT]
  Power = LED - 3mm [color="Red (635nm)" package="3 mm [THT]"]
  300 = Resistor [tolerance=±5% resistance=220 package=THT]
  300_2 = Resistor [tolerance=±5% resistance=220 package=THT]
  300_3 = Resistor [tolerance=±5% resistance=220 package=THT]
  JP8 = Header 1 [package=1x01_offset]
  JP15 = Header 1 [package=1x01_offset]

nets:
  N1: JP4.1, JP5.1, JP9.1, JP12.1, JP13.1, 0_1.1, 0_1_2.1, Part1.GND, 0_1_3.1, 2YOA21.2, 2YOA21_2.2, Bat.pin2, Power.cathode, JP8.1
  N2: QRB1134.1, 0_1_2.2, Part1.A2
  N3: JP7.1, 220_2.Pin_1
  N4: QRB1134_2.1, 0_1.2, Part1.A1, 10k_2.Pin_1
  N5: JP11.1, 220.Pin_1
  N6: QRB1134_3.1, Part1.A0, 0_1_3.2, 10k.Pin_1
  N7: 11.cathode, 300_3.Pin_0
  N8: 11.anode, Part1.D11_PWM
  N9: Part1.5V, 10k.Pin_0, 220.Pin_0, 10k_2.Pin_0, 220_2.Pin_0, 10k_3.Pin_0, 2YOA21.1, 2YOA21_2.1, 220_3.Pin_1
  N10: Part1.A3, 2YOA21.3
  N11: Part1.A4, 2YOA21_2.3
  N12: Part1.D12/A11, 12.anode
  N13: Part1.D13_PWM, 13.anode
  N14: 13.cathode, 300.Pin_0
  N15: 12.cathode, 300_2.Pin_0
  N16: Bat.pin1, On_Off.O, On_Off.P
  N17: 470.Pin_0, On_Off.S
  N18: 470.Pin_1, Power.anode, 300.Pin_1, 300_2.Pin_1, 300_3.Pin_1
  N19: 220_3.Pin_0, JP15.1
